# Fritzing sketch EDS-EarthquakeDetectionSystem (saved by Fritzing 0.9.10b)
circuit board: 25.6835cm x 16.4169cm
stripboards: 2

parts:
  Part2 = Arduino Uno (Rev3)
  ADXL3 = ADXL335 Accelerometer Breakout
  LCD2 = LCD screen
  LCM1602_IIC3 = LCM1602 IIC [part_number="LCM1602 IIC" chip_label="LCM1602 IIC" package="DIP (Dual Inline) [THT]"]
  LED2 = smd LED [color="Red (633nm)" package="0805 [SMD]"]
  R1 = Resistor [tolerance=±5% resistance=220 package="0603 [SMD]"]
  R2 = Resistor [tolerance=±5% resistance=220 package="2010 [SMD]"]
  J2 = Piezo Speaker
  U1 = ESP8266 WiFi Module [part_number=ESP8266]
  C2 = Capacitor Polarized [package=cpol-radial-100uf-25v]
  R3 = Resistor [tolerance=±5% resistance=1k package="0603 [SMD]"]
  R4 = Resistor [tolerance=±5% resistance=1k package="0603 [SMD]"]
  R5 = Resistor [tolerance=±5% resistance=1k package="0603 [SMD]"]

nets:
  N1: Part2.A0, ADXL3.Zout
  N2: Part2.A1, ADXL3.Yout
  N3: Part2.A2, ADXL3.Xout
  N4: Part2.A4/SDA, LCM1602_IIC3.SDA
  N5: Part2.A5/SCL, LCM1602_IIC3.SCL
  N6: Part2.D8, LED2.anode
  N7: Part2.D10_PWM/SS, U1.TXD
  N8: Part2.D11_PWM/MOSI, R3.Pin_1
  GND: Part2.D12/MISO, Part2.GND, LCM1602_IIC3.GND, LED2.cathode, R2.Pin_0, R2.Pin_1, J2.pin2, U1.GND, C2.-, R5.Pin_0
  3V3: Part2.3V3, U1.VCC, U1.CH_PD, C2.+
  5V: Part2.5V, ADXL3.Vin, LCM1602_IIC3.VCC
  N9: ADXL3.GND, J2.pin1
  VSS: LCD2.VSS, LCM1602_IIC3.VSS
  VDD: LCD2.VDD, LCM1602_IIC3.VDD
  N10: LCD2.V0, LCM1602_IIC3.V0
  N11: LCD2.RS, LCM1602_IIC3.RS
  N12: LCD2.R/W, LCM1602_IIC3.RW
  N13: LCD2.E, LCM1602_IIC3.E
  N14: LCD2.DB0, LCM1602_IIC3.D0
  N15: LCD2.DB1, LCM1602_IIC3.D1
  N16: LCD2.DB2, LCM1602_IIC3.D2
  N17: LCD2.DB3, LCM1602_IIC3.D3
  N18: LCD2.DB4, LCM1602_IIC3.D4
  N19: LCD2.DB5, LCM1602_IIC3.D5
  N20: LCD2.DB6, LCM1602_IIC3.D6
  N21: LCD2.DB7, LCM1602_IIC3.D7
  N22: LCD2.LED+, LCM1602_IIC3.A
  N23: LCD2.LED-, LCM1602_IIC3.K
  N24: LCM1602_IIC3.LED_A, LCM1602_IIC3.LED_B, R1.Pin_0, R1.Pin_1
  N25: U1.RXD, R3.Pin_0, R4.Pin_1
  N26: R4.Pin_0, R5.Pin_1

custom parts:
  ADXL335 Accelerometer Breakout: ADXL335 Accelerometer Breakout board
  LCM1602 IIC: I2C-Module to use a 1602 or 2004 LCD on with the wire.h libory Serial LCD Modul
  ESP8266 WiFi Module: Generic WiFi Module based on the ESP8266 with onboard PCB antenna and UART communications

// code stored in the sketch: Code.ino


// code stored in the sketch: EDS-EarthquakeDetectionSystem.ino
/*Earthquake Detector V1.0 

Designed By Boran ATILGAN*/

//NOTE: Please add melodiesandpins.h library inside the folder.Otherwise, software errors may occur.

#include <math.h>
#include <LiquidCrystal_I2C.h>
#include "melodiesandpins.h"

LiquidCrystal_I2C lcd(0x27,16,2); 
int maxvalx = 327,minvalx = 315;
int maxvaly = 330,minvaly = 300;
  
void setup()
{
  Serial.begin(9600);
  pinMode(buzzerPin,OUTPUT);
  pinMode(ledPin,OUTPUT);
  lcd.begin();


{
  for (int i = 0; i < toneNumber; i++)
  {
    tone(buzzerPin, notes[i]);
    delay(100);
    noTone(buzzerPin);
    delay(20);
  }
  noTone(buzzerPin);
}  
delay(100);
lcd.setCursor(0,0);
lcd.print("Earthquake");
lcd.setCursor(0,1);
lcd.print("Detector 1.0");
delay(2000);
lcd.clear();

lcd.setCursor(0,0);
lcd.print("Calibrating The");
lcd.setCursor(0,1);
lcd.print("System");
delay(3000);
lcd.clear();

lcd.setCursor(0,0);
lcd.print("Calibrating");
lcd.setCursor(0,1);
lcd.print("*");
delay(2000);
lcd.print("*");
delay(2000);
lcd.print("*");

delay(3000);
lcd.clear();

lcd.setCursor(0,0);
lcd.print("Calibration");
lcd.setCursor(0,1);
lcd.print("Completed");
delay(3000);
lcd.clear();
  }

  void loop(){

int x_rawvalue, y_rawvalue, z_rawvalue; 
  double x_g_value, y_g_value, z_g_value;
  double roll, pitch, yaw;
  x_rawvalue = analogRead(xPin); /* Digital value of voltage on x_out pin */ 
  y_rawvalue = analogRead(yPin); /* Digital value of voltage on y_out pin */ 
  z_rawvalue = analogRead(zPin); /* Digital value of voltage on z_out pin */ 
  Serial.print("x = ");
  Serial.print(x_rawvalue);
  Serial.print("\t\t");
  Serial.print("y = ");
  Serial.print(y_rawvalue);
  Serial.print("\t\t");
  Serial.print("z = ");
  Serial.print(z_rawvalue);
  Serial.print("\t\t");

  
  x_g_value = ( ( ( (double)(x_rawvalue * 5)/1024) - 1.65 ) / 0.330 ); /* Acceleration in x-direction in g units */ 
  y_g_value = ( ( ( (double)(y_rawvalue * 5)/1024) - 1.65 ) / 0.330 ); /* Acceleration in y-direction in g units */ 
  z_g_value = ( ( ( (double)(z_rawvalue * 5)/1024) - 1.80 ) / 0.330 ); /* Acceleration in z-direction in g units */ 

  roll = ( ( (atan2(y_g_value,z_g_value) * 180) / 3.14 ) + 180 ); /* Formula for roll */
  pitch = ( ( (atan2(z_g_value,x_g_value) * 180) / 3.14 ) + 180 ); /* Formula for pitch */
  yaw = ( ( (atan2(x_g_value,y_g_value) * 180) / 3.14 ) + 180 ); /* Formula for yaw */
  /* Not possible to measure yaw using accelerometer. Gyroscope must be used if yaw is also required */

  Serial.print("Roll = ");
  Serial.print(roll);
  Serial.print("\t");
  Serial.print("Pitch = ");
  Serial.print(pitch);
  Serial.print("\n\n");
  delay(300);

  lcd.clear();

  
 if(x_rawvalue > maxvalx || x_rawvalue<minvalx)

 {

  lcd.clear();
  digitalWrite(buzzerPin,LOW);
  lcd.setCursor(0,0);
  lcd.print("Earthquake");
  lcd.setCursor(0,1);
  lcd.print("Alert");
  digitalWrite(buzzerPin,HIGH);
  delay(10);
  digitalWrite(buzzerPin,LOW);
  delay(10);
  digitalWrite(ledPin,HIGH);
  delay(10);
  digitalWrite(ledPin,LOW);
  delay(10);
 }
else if(y_rawvalue>maxvaly || y_rawvalue<minvaly)
 {
 
  digitalWrite(buzzerPin,LOW);
  delay(5);
  lcd.clear();
  lcd.setCursor(0,0);
  lcd.print("Earthquake");
  lcd.setCursor(0,1);
  lcd.print("Alert");
  digitalWrite(buzzerPin,HIGH);
  delay(5);
  digitalWrite(buzzerPin,LOW);
  delay(5);
  digitalWrite(ledPin,HIGH);
  delay(5);
  digitalWrite(ledPin,LOW);
  delay(5);
  }
  
 else
 {

  digitalWrite(buzzerPin,LOW);
  digitalWrite(ledPin,LOW);
  delay(5);
  lcd.clear();
  lcd.setCursor(0,0);
  lcd.print("No Shake");
  lcd.setCursor(0,1);
  lcd.print("Detected");
  
  }
}
